# Fritzing sketch 配線 (saved by Fritzing 0.9.4)
breadboards: 1

parts:
  part = Arduino Uno (Rev3)
  R1 = Resistor [tolerance=±5% resistance=220 package="0402 [SMD]"]
  S1 = Momentary Switch [package=ksa_sealed_tac_switch]
  S2 = Momentary Switch [package=ksa_sealed_tac_switch]
  S3 = Momentary Switch [package=ksa_sealed_tac_switch]
  S4 = Momentary Switch [package=ksa_sealed_tac_switch]
  S5 = Momentary Switch [package=ksa_sealed_tac_switch]
  R2 = Resistor [tolerance=±5% resistance=220 package="0402 [SMD]"]
  R3 = Resistor [tolerance=±5% resistance=220 package="0402 [SMD]"]
  R4 = Resistor [tolerance=±5% resistance=220 package="0402 [SMD]"]
  R5 = Resistor [tolerance=±5% resistance=220 package="0402 [SMD]"]
  D1 = LTE-302 [package=lte-302]
  Gizwits_WiFi_Witty_ESP-12F1 = Gizwits WiFi Witty ESP-12F

nets:
  N1: part.D8, S3.3, R3.Pin_1
  N2: part.D12/MISO, S2.3, R2.Pin_1
  N3: part.D0/RX, Gizwits_WiFi_Witty_ESP-12F1.RXD
  N4: part.D1/TX, Gizwits_WiFi_Witty_ESP-12F1.TXD
  N5: part.D2, R1.Pin_1, S1.3
  N6: part.D3_PWM, D1.A
  N7: part.D4, S5.3, R5.Pin_1
  N8: part.D7, S4.3, R4.Pin_1
  3V3: part.3V3, Gizwits_WiFi_Witty_ESP-12F1.CH_PD, Gizwits_WiFi_Witty_ESP-12F1.VCC
  N9: part.5V, R1.Pin_0, R2.Pin_0, R3.Pin_0, R4.Pin_0, R5.Pin_0
  GND: part.GND, S1.1, S2.1, S3.1, S4.1, S5.1, D1.C, Gizwits_WiFi_Witty_ESP-12F1.GND
